# Fritzing sketch drone-schematic (saved by Fritzing 1.0.4)
breadboards: 1

parts:
  BAT1 = Battery Holders [package=lipo-1100mAh]  # not connected
  920KV_Motor1 = DJI 920 KV Motor
  M1 = ESC
  920KV_Motor2 = DJI 920 KV Motor
  M2 = ESC
  Part1 = InvenSense MPU6050
  A1 = Teensy 4.0

nets:
  N1: 920KV_Motor1.w, M1.W
  N2: 920KV_Motor1.v, M1.V
  N3: 920KV_Motor1.u, M1.U
  GND: M1.GND, M2.GND, Part1.GND, A1.pin_1, A1.pin_32
  N4: 920KV_Motor2.w, M2.W
  N5: 920KV_Motor2.v, M2.V
  N6: 920KV_Motor2.u, M2.U

custom parts:
  DJI 920 KV Motor: DJI Brushless Outrunner 2212/920K Motor F330-550
  Teensy 4.0: The Teensy is a complete USB-based microcontoller development system, in a very small footprint, capable of implementing many types of projects. All programming is done via the USB port. No special programmer is needed, only a standard micro-USB cable and a PC or Macintosh with a USB port. (Oct 2023 added the VBUS pad at user request.)
